# Fritzing sketch TMC2130 SPI (saved by Fritzing 0.9.3b)
circuit board: 6.32866cm x 2.58362cm
breadboards: 1

parts:
  E0 = female pin header, 4 pins [form="♀ (female)"]
  X = female pin header, 4 pins [form="♀ (female)"]
  Y = female pin header, 4 pins [form="♀ (female)"]
  Z = female pin header, 4 pins [form="♀ (female)"]
  E1 = female pin header, 4 pins [form="♀ (female)"]
  CS = female pin header, 5 pins [form="♀ (female)"]
  SPI = female pin header, 3 pins [form="♀ (female)"]

nets:
  N1: E0.pin1, X.pin1, Y.pin1, Z.pin1, E1.pin1, SPI.pin3
  N2: E0.pin2, X.pin2, Y.pin2, Z.pin2, E1.pin2, SPI.pin2
  N3: E0.pin3, CS.pin2
  N4: E0.pin4, X.pin4, Y.pin4, Z.pin4, E1.pin4, SPI.pin1
  N5: X.pin3, CS.pin5
  N6: Y.pin3, CS.pin4
  N7: Z.pin3, CS.pin3
  N8: E1.pin3, CS.pin1

notes:
  X
  Z
  Y
  E0
  E1
  TMC2130 SPI
  Breakout Board
  SDI
  SCK
  SDO
  By Thomas Bladykas
